# Fritzing sketch ldr street light (saved by Fritzing 0.9.3b)
breadboards: 1

parts:
  R1 = Photocell (LDR) [package=THT]
  LED1 = smd LED [color="Red (633nm)" package="1206 [SMD]"]
  R2 = Resistor [tolerance=±5% resistance=330 package="2010 [SMD]"]
  R3 = Resistor [tolerance=±5% resistance=10k package="2010 [SMD]"]
  Part1 = Arduino Uno (Rev3) - ICSP

nets:
  N1: R1.pin_0, Part1.5V
  N2: R1.pin_1, R3.Pin_1, Part1.A5/SCL
  N3: LED1.cathode, R2.Pin_1
  N4: LED1.anode, Part1.D2
  N5: R2.Pin_0, R3.Pin_0, Part1.GND

notes:
  R1 330 Ω
  R2 10kΩ
